# Fritzing sketch sketch (saved by Fritzing 0.9.3b)

parts:
  U4 = SUP500F [package=sup500f]
  Grove1 = Grove 3 Axis Digital Accelerometer 16g
  Raspberry_Pi_1 = Raspberry Pi 3 [part_number=RPI-3-V1.2]

nets:
  N1: U4.RX-I, Raspberry_Pi_1.GPIO14
  N2: U4.TX-O, Raspberry_Pi_1.GPIO15
  GND: U4.GND, Grove1.GND, Raspberry_Pi_1.GND
  VCC: U4.VCC, Grove1.VCC, Raspberry_Pi_1.5V
  N3: Grove1.SDA, Raspberry_Pi_1.GPIO2
  N4: Grove1.SCL, Raspberry_Pi_1.GPIO3
